# Fritzing sketch AttendanceCircuit.sys (saved by Fritzing 0.9.3b)

parts:
  Part1 = RFID-RC522-v2
  U1 = ESP8266 NodeMCU LoLin module
  LED1 = LED - 5mm [color="Red (633nm)" package="5 mm [THT]"]
  LED2 = LED - 5mm [color="Yellow (595nm)" package="5 mm [THT]"]
  LED3 = LED - 5mm [color="Green (565nm)" package="5 mm [THT]"]

nets:
  N1: Part1.SDA, U1.D4
  N2: Part1.SCK, U1.D5
  N3: Part1.MOSI, U1.D7
  N4: Part1.MISO, U1.D6
  GND: Part1.GND, U1.GND, LED1.cathode, LED2.cathode, LED3.cathode
  N5: Part1.RST, U1.D3
  3.3V: Part1.3.3V, U1.3V3
  N6: U1.D0, LED1.anode
  N7: U1.D1, LED2.anode
  N8: U1.D2, LED3.anode

custom parts:
  RFID-RC522-v2: A simple China made RFID-RC522 Reader; do check the pin labels, as this is a MFRC522 based clone.
  ESP8266 NodeMCU LoLin module: ESP8266 based NodeMCU
